// Logisim project circuits.circ as structural Verilog: 9 circuits, main circuit chipotle
module sleeping (
  input  Lecture_is_Exciting,
  input  Got_enough_sleep,
  output Am_I_asleep,
  output Am_I_asleep_2
);

  wire not_1_out, not_2_out, or_1_out;

  not not_1 (not_1_out, Lecture_is_Exciting);
  not not_2 (not_2_out, Got_enough_sleep);
  or or_1 (or_1_out, Lecture_is_Exciting, Got_enough_sleep);
  and and_1 (Am_I_asleep, not_1_out, not_2_out);
  not not_3 (Am_I_asleep_2, or_1_out);
endmodule

module chipotle (
  input  Chipotle_is_Open,
  input  Hungry,
  input  Have_food_in_apartment,
  output Eat_at_Chipotle
);

  wire and_1_out, not_1_out;

  not not_1 (not_1_out, Have_food_in_apartment);
  and and_1 (and_1_out, Chipotle_is_Open, Hungry);
  and and_2 (Eat_at_Chipotle, and_1_out, not_1_out);
endmodule

module pav (
  input  [2:0] People_in_Line,
  output Should_close_the_line
);

  and and_1 (Should_close_the_line, People_in_Line[1], People_in_Line[2]);
endmodule

module encoder (
  input  Line_0,
  input  Line_1,
  input  in_3,
  input  in_4,
  input  in_5,
  input  in_6,
  output Highest_Line_On,
  output Any_Line_On,
  output Highest_Line_On__1_digit,
  output Highest_Line_On__2_digit,
  output Any_Line_On_2
);

  wire and_1_out, not_3_out, or_2_out, or_4_out;

  // NOT_Gate not_1 has open pins: in=in_3, out=open
  // NOT_Gate not_2 has open pins: in=in_4, out=open
  not not_3 (not_3_out, in_5);
  // NOT_Gate not_4 has open pins: in=in_6, out=open
  or or_1 (Any_Line_On, Line_0, Line_1);
  or or_2 (or_2_out, in_3, in_4);
  or or_3 (Any_Line_On_2, or_2_out, or_4_out);
  or or_4 (or_4_out, in_5, in_6);
  and and_1 (and_1_out, in_4, not_3_out);
  or or_5 (Highest_Line_On__1_digit, and_1_out, in_6);
  or or_6 (Highest_Line_On__2_digit, in_5, in_6);

  assign Highest_Line_On = Line_1;
endmodule

module muxer (
  input  Line_0,
  input  Line_1,
  input  Control,
  output Muxed_Output
);

  wire and_1_out, and_2_out, not_3_out;

  // NOT_Gate not_1 has open pins: in=Line_0, out=open
  // NOT_Gate not_2 has open pins: in=Line_1, out=open
  not not_3 (not_3_out, Control);
  and and_1 (and_1_out, not_3_out, Line_0);
  and and_2 (and_2_out, Line_1, Control);
  or or_1 (Muxed_Output, and_1_out, and_2_out);
endmodule

module half_adder (
  input  A,
  input  B,
  input  A_2,
  input  B_2,
  output A___B,
  output Cout,
  output A___B_2,
  output Cout_2
);

  wire and_3_out, not_1_out, or_1_out;

  and and_1 (Cout, B, A);
  and and_2 (Cout_2, B_2, A_2);
  xor xor_1 (A___B, A, B);
  and and_3 (and_3_out, A_2, B_2);
  not not_1 (not_1_out, and_3_out);
  or or_1 (or_1_out, A_2, B_2);
  and and_4 (A___B_2, not_1_out, or_1_out);
endmodule

module full_adder (
  input  A,
  input  B,
  input  Cin,
  output A___B,
  output Cout
);

  wire and_1_out, and_2_out, xor_1_out;

  xor xor_1 (xor_1_out, A, B);
  xor xor_2 (A___B, xor_1_out, Cin);
  and and_1 (and_1_out, xor_1_out, Cin);
  and and_2 (and_2_out, B, A);
  or or_1 (Cout, and_1_out, and_2_out);
endmodule

module ripple_carry (
  input  [7:0] A__8_bit,
  input  [7:0] B__8_bit,
  output [7:0] A___B,
  output Cout
);

  wire full_adder_1_cout, full_adder_2_cout, full_adder_3_cout, full_adder_4_cout, full_adder_5_cout,
       full_adder_6_cout, full_adder_7_cout;

  full_adder full_adder_1 (.A(A__8_bit[0]), .B(B__8_bit[0]), .Cin(1'b0), .A___B(A___B[0]), .Cout(full_adder_1_cout));
  full_adder full_adder_2 (
    .A(A__8_bit[1]), .B(B__8_bit[1]), .Cin(full_adder_1_cout), .A___B(A___B[1]), .Cout(full_adder_2_cout));
  full_adder full_adder_3 (
    .A(A__8_bit[2]), .B(B__8_bit[2]), .Cin(full_adder_2_cout), .A___B(A___B[2]), .Cout(full_adder_3_cout));
  full_adder full_adder_4 (
    .A(A__8_bit[3]), .B(B__8_bit[3]), .Cin(full_adder_3_cout), .A___B(A___B[3]), .Cout(full_adder_4_cout));
  full_adder full_adder_5 (
    .A(A__8_bit[4]), .B(B__8_bit[4]), .Cin(full_adder_4_cout), .A___B(A___B[4]), .Cout(full_adder_5_cout));
  full_adder full_adder_6 (
    .A(A__8_bit[5]), .B(B__8_bit[5]), .Cin(full_adder_5_cout), .A___B(A___B[5]), .Cout(full_adder_6_cout));
  full_adder full_adder_7 (
    .A(A__8_bit[6]), .B(B__8_bit[6]), .Cin(full_adder_6_cout), .A___B(A___B[6]), .Cout(full_adder_7_cout));
  full_adder full_adder_8 (.A(A__8_bit[7]), .B(B__8_bit[7]), .Cin(full_adder_7_cout), .A___B(A___B[7]), .Cout(Cout));

  // Notes on the sheet:
  //   Our Full Adders
endmodule

module sr_latch (
  input  S,
  input  R,
  output Q,
  output not_Q
);

  nand nand_1 (Q, S, not_Q);
  nand nand_2 (not_Q, Q, R);
endmodule
