// Logisim project processor.circ as structural Verilog: 2 circuits, main circuit alu
module alu (
  input  [2:0] control,
  input  [7:0] a,
  input  [7:0] b,
  output [7:0] Output
);

  wire [7:0] adder_1_out, comparator_1_eq, comparator_1_gt, comparator_1_lt, divider_1_out, multiplier_1_out,
       subtractor_1_out;

  Adder adder_1 (.a(a), .b(b), .out(adder_1_out));  // open: cin, cout
  Multiplier multiplier_1 (.a(a), .b(b), .out(multiplier_1_out));  // open: cin, cout
  Subtractor subtractor_1 (.a(a), .b(b), .out(subtractor_1_out), .bin(1'b0));  // open: bout
  Divider divider_1 (.a(a), .b(b), .out(divider_1_out));  // open: upper, rem
  Comparator comparator_1 (.a(a), .b(b), .gt(comparator_1_gt[0]), .eq(comparator_1_eq[0]), .lt(comparator_1_lt[0]));
  Multiplexer #(.select(3), .width(8)) multiplexer_1 (
    .in0(adder_1_out), .in1(multiplier_1_out), .in2(subtractor_1_out), .in3(divider_1_out),
    .in4(comparator_1_gt), .in5(comparator_1_eq), .in6(comparator_1_lt), .out(Output), .sel(control));  // open: in7, en
endmodule

module registerfile (
  input  [7:0] data,
  input  [1:0] register_num,
  input  write,
  input  [1:0] in_4,
  output [7:0] Output
);

  wire clock_1_out, decoder_1_out0, decoder_1_out1, decoder_1_out2;
  wire [7:0] multiplexer_1_out, multiplexer_2_out, multiplexer_3_out, register_1_q, register_2_q,
       register_3_q;

  Decoder #(.select(2)) decoder_1 (
    .out0(decoder_1_out0), .out1(decoder_1_out1), .out2(decoder_1_out2), .sel(register_num), .en(write));  // open: out3
  Clock clock_1 (.out(clock_1_out));
  Multiplexer #(.width(8), .enable("false")) multiplexer_1 (
    .in0(register_1_q), .in1(data), .out(multiplexer_1_out), .sel(decoder_1_out0));
  Multiplexer #(.width(8), .enable("false")) multiplexer_2 (
    .in0(register_2_q), .in1(data), .out(multiplexer_2_out), .sel(decoder_1_out1));
  Multiplexer #(.width(8), .enable("false")) multiplexer_3 (
    .in0(register_3_q), .in1(data), .out(multiplexer_3_out), .sel(decoder_1_out2));
  Register register_1 (.D(multiplexer_1_out), .Q(register_1_q), .clk(clock_1_out));  // open: en, clr
  Register register_2 (.D(multiplexer_2_out), .Q(register_2_q), .clk(clock_1_out));  // open: en, clr
  Register register_3 (.D(multiplexer_3_out), .Q(register_3_q), .clk(clock_1_out));  // open: en, clr
  Multiplexer #(.select(2), .width(8)) multiplexer_4 (
    .in0(register_1_q), .in1(register_2_q), .in2(register_3_q), .in3({8{1'b0}}), .out(Output), .sel(in_4));  // open: en
endmodule
