// Logisim project state.circ as structural Verilog: 3 circuits, main circuit simple
module simple (
  input  in_1,
  output out_2
);

  wire clock_1_out;

  Clock clock_1 (.out(clock_1_out));
  D_Flip_Flop d_ff_1 (.clk(clock_1_out), .D(in_1), .Q(out_2));  // open: Qn, preset, en, reset
endmodule

module counter (
  input  Someone_in_line,
  input  Reset,
  output Should_close_line
);

  wire clock_1_out;
  wire [7:0] adder_1_out, register_1_q;

  Register register_1 (.D(adder_1_out), .Q(register_1_q), .clk(clock_1_out), .clr(Reset));  // open: en
  Clock clock_1 (.out(clock_1_out));
  Adder adder_1 (.a({{7{1'b0}}, Someone_in_line}), .b(register_1_q), .out(adder_1_out), .cin(1'b0));  // open: cout
  Comparator comparator_1 (.a(register_1_q), .b(8'h5), .gt(Should_close_line));  // open: eq, lt
endmodule

module counter3 (
  input  Someone_in_line,
  input  Reset,
  input  Extra_Staff,
  output Should_close_line
);

  wire clock_1_out;
  wire [7:0] adder_1_out, multiplexer_1_out, register_1_q;

  Register register_1 (.D(adder_1_out), .Q(register_1_q), .clk(clock_1_out), .clr(Reset));  // open: en
  Clock clock_1 (.out(clock_1_out));
  Adder adder_1 (.a({{7{1'b0}}, Someone_in_line}), .b(register_1_q), .out(adder_1_out), .cin(1'b0));  // open: cout
  Multiplexer #(.width(8), .enable("false")) multiplexer_1 (
    .in0(8'h5), .in1(8'ha), .out(multiplexer_1_out), .sel(Extra_Staff));
  Comparator comparator_1 (.a(register_1_q), .b(multiplexer_1_out), .gt(Should_close_line));  // open: eq, lt
endmodule
